// Logisim project pong.circ as structural Verilog: 4 circuits, main circuit main
module main (
);

  wire and_1_out, and_2_out, and_3_out, Clk, clock_1_out, comparator_1_gt, comparator_2_lt, comparator_3_lt,
       comparator_4_lt, comparator_5_gt, comparator_5_lt, comparator_6_lt, comparator_7_eq, comparator_8_gt,
       comparator_9_lt, comparator_10_eq, comparator_11_eq, Lose, not_1_out, or_1_out;
  wire [2:0] counter_1_q;
  wire [3:0] adder_3_out, adder_4_out, ScoreA, ScoreB;
  wire [4:0] A, adder_1_out, adder_2_out, adder_5_out, adder_6_out, adder_7_out, Ay, B, By, truc_1_value,
       truc_2_value;
  wire [23:0] demultiplexer_1_out0, demultiplexer_1_out1, demultiplexer_1_out2, demultiplexer_1_out3,
       demultiplexer_1_out4, demultiplexer_1_out5, demultiplexer_1_out6, demultiplexer_1_out7,
       demultiplexer_1_out8, demultiplexer_1_out9, demultiplexer_1_out10, demultiplexer_1_out11,
       demultiplexer_1_out12, demultiplexer_1_out13, demultiplexer_1_out14, demultiplexer_1_out15,
       demultiplexer_1_out16, demultiplexer_1_out17, demultiplexer_1_out18, demultiplexer_1_out19,
       demultiplexer_1_out20, demultiplexer_1_out21, demultiplexer_1_out22, demultiplexer_1_out23,
       demultiplexer_1_out24, demultiplexer_1_out25, demultiplexer_1_out26, demultiplexer_1_out27,
       demultiplexer_1_out28, demultiplexer_1_out29, demultiplexer_1_out30, digit_1_c1, digit_1_c2,
       digit_1_c3, digit_2_c1, digit_2_c2, digit_2_c3, or_3_out, or_4_out, or_5_out, or_6_out, or_7_out,
       or_8_out, or_9_out, or_10_out, or_11_out, or_12_out, or_13_out, or_14_out, or_15_out, or_16_out,
       or_17_out, or_18_out, or_19_out, or_20_out, or_21_out, or_22_out, or_23_out, or_24_out, or_25_out,
       or_26_out, or_27_out, or_28_out, or_29_out, or_30_out, or_31_out, or_32_out, or_33_out, shifter_1_out,
       shifter_2_out, shifter_3_out;

  Adder #(.width(5)) adder_1 (.a(By), .b(5'b01000), .out(adder_1_out));  // open: cin, cout
  Comparator #(.width(5)) comparator_1 (.a(truc_2_value), .b(5'b01100), .gt(comparator_1_gt));  // open: eq, lt
  Adder #(.width(5)) adder_2 (.a(Ay), .b(5'b01000), .out(adder_2_out));  // open: cin, cout
  Comparator #(.width(5)) comparator_2 (.a(truc_2_value), .b(5'b10100), .lt(comparator_2_lt));  // open: gt, eq
  Adder #(.width(4)) adder_3 (.a(ScoreA), .b(4'b0001), .out(adder_3_out));  // open: cin, cout
  Counter #(.max('h7), .width(3)) counter_1 (
    .load(Lose), .D(3'b110), .Q(counter_1_q), .up(1'b0), .clk(or_1_out));  // open: count, carry, clr
  or or_1 (or_1_out, Lose, and_1_out);
  and and_1 (and_1_out, clock_1_out, not_1_out);
  Clock clock_1 (.out(clock_1_out));
  Comparator #(.mode("unsigned"), .width(5)) comparator_3 (
    .a(adder_7_out), .b(By), .lt(comparator_3_lt));  // open: gt, eq
  and and_2 (and_2_out, ~comparator_3_lt, comparator_4_lt, comparator_1_gt);  // AND_Gate
  Comparator #(.mode("unsigned"), .width(5)) comparator_4 (
    .a(adder_7_out), .b(adder_1_out), .lt(comparator_4_lt));  // open: gt, eq
  Comparator #(.mode("unsigned"), .width(5)) comparator_5 (
    .a(adder_7_out), .b(Ay), .gt(comparator_5_gt), .lt(comparator_5_lt));  // open: eq
  Comparator #(.mode("unsigned"), .width(5)) comparator_6 (
    .a(adder_7_out), .b(adder_2_out), .lt(comparator_6_lt));  // open: gt, eq
  and and_3 (and_3_out, ~comparator_5_lt, comparator_6_lt, comparator_2_lt);  // AND_Gate
  Register #(.width(4)) register_1 (
    .D(adder_3_out), .en(comparator_10_eq), .clk(comparator_10_eq), .Q(ScoreA));  // open: clr
  Comparator #(.width(3)) comparator_7 (.a(counter_1_q), .b(3'b000), .eq(comparator_7_eq));  // open: gt, lt
  Comparator #(.width(5)) comparator_8 (.a(truc_1_value), .b(5'b01011), .gt(comparator_8_gt));  // open: eq, lt
  Comparator #(.width(5)) comparator_9 (.a(truc_1_value), .b(5'b10110), .lt(comparator_9_lt));  // open: gt, eq
  not not_1 (not_1_out, comparator_7_eq);
  // Buzzer #(.waveform("Square")) buzzer_1: pin names not known; wires that end beside it: 14'hf3, not_1_out, {7{1'b1}}
  and and_4 (Clk, ~not_1_out, clock_1_out);  // AND_Gate
  Register #(.width(4)) register_2 (
    .D(adder_4_out), .en(comparator_11_eq), .clk(comparator_11_eq), .Q(ScoreB));  // open: clr
  Adder #(.width(4)) adder_4 (.a(ScoreB), .b(4'b0001), .out(adder_4_out));  // open: cin, cout
  truc truc_1 (
    .Value(truc_1_value), .Cond1(comparator_8_gt), .Cond2(comparator_9_lt), .Lose(Lose), .Clk(Clk),
    .in_5(14'hf5));
  truc truc_2 (.Value(truc_2_value), .Cond1(and_2_out), .Cond2(and_3_out), .Lose(Lose), .Clk(Clk), .in_5(14'h1e5));
  paddleCtl paddlectl_1 (.PaddleY(Ay), .JoyY(A), .Lose(Lose));
  Adder #(.width(5)) adder_5 (.a(5'b01011), .b(truc_1_value), .out(adder_5_out));  // open: cin, cout
  Adder #(.width(5)) adder_6 (.a(5'b01111), .b(truc_2_value), .out(adder_6_out));  // open: cin, cout
  Comparator #(.width(5)) comparator_10 (.a(5'b01111), .b(truc_2_value), .eq(comparator_10_eq));  // open: gt, lt
  or or_2 (Lose, comparator_10_eq, comparator_11_eq);
  Comparator #(.width(5)) comparator_11 (.a(5'b10001), .b(truc_2_value), .eq(comparator_11_eq));  // open: gt, lt
  paddleCtl paddlectl_2 (.PaddleY(By), .JoyY(B), .Lose(Lose));
  Shifter #(.width(24)) shifter_1 (.in(24'h3f), .\dist (Ay), .out(shifter_1_out));
  Demultiplexer #(.enable("false"), .select(5), .width(24)) demultiplexer_1 (
    .out0(demultiplexer_1_out0), .out1(demultiplexer_1_out1), .out2(demultiplexer_1_out2),
    .out3(demultiplexer_1_out3), .out4(demultiplexer_1_out4), .out5(demultiplexer_1_out5),
    .out6(demultiplexer_1_out6), .out7(demultiplexer_1_out7), .out8(demultiplexer_1_out8),
    .out9(demultiplexer_1_out9), .out10(demultiplexer_1_out10), .out11(demultiplexer_1_out11),
    .out12(demultiplexer_1_out12), .out13(demultiplexer_1_out13), .out14(demultiplexer_1_out14),
    .out15(demultiplexer_1_out15), .out16(demultiplexer_1_out16), .out17(demultiplexer_1_out17),
    .out18(demultiplexer_1_out18), .out19(demultiplexer_1_out19), .out20(demultiplexer_1_out20),
    .out21(demultiplexer_1_out21), .out22(demultiplexer_1_out22), .out23(demultiplexer_1_out23),
    .out24(demultiplexer_1_out24), .out25(demultiplexer_1_out25), .out26(demultiplexer_1_out26),
    .out27(demultiplexer_1_out27), .out28(demultiplexer_1_out28), .out29(demultiplexer_1_out29),
    .out30(demultiplexer_1_out30), .in(shifter_2_out), .sel(adder_6_out));  // open: out31
  Shifter #(.width(24)) shifter_2 (.in(24'h1), .\dist (adder_5_out), .out(shifter_2_out));
  Adder #(.width(5)) adder_7 (.a(adder_5_out), .b(5'b00001), .out(adder_7_out));  // open: cin, cout
  Shifter #(.width(24)) shifter_3 (.in(24'h3f), .\dist (By), .out(shifter_3_out));
  digit digit_1 (.C1(digit_1_c1), .C2(digit_1_c2), .C3(digit_1_c3), .Score(ScoreA));
  digit digit_2 (.C1(digit_2_c1), .C2(digit_2_c2), .C3(digit_2_c3), .Score(ScoreB));
  Joystick #(.bits(5)) joystick_1 (.y(A));  // open: x
  DotMatrix #(.matrixcols(31), .matrixrows(24)) dotmatrix_1 (
    .col0(or_3_out), .col1(or_4_out), .col2(or_5_out), .col3(or_6_out), .col4(or_7_out), .col5(or_8_out),
    .col6(or_9_out), .col7(or_10_out), .col8(or_11_out), .col9(or_12_out), .col10(or_13_out),
    .col11(or_14_out), .col12(or_15_out), .col13(or_16_out), .col14(or_17_out), .col15(or_18_out),
    .col16(or_19_out), .col17(or_20_out), .col18(or_21_out), .col19(or_22_out), .col20(or_23_out),
    .col21(or_24_out), .col22(or_25_out), .col23(or_26_out), .col24(or_27_out), .col25(or_28_out),
    .col26(or_29_out), .col27(or_30_out), .col28(or_31_out), .col29(or_32_out), .col30(or_33_out));
  assign or_3_out = {24{1'b0}} | demultiplexer_1_out0;  // OR_Gate or_3, 24 bits wide
  assign or_4_out = shifter_1_out | demultiplexer_1_out1;  // OR_Gate or_4, 24 bits wide
  assign or_5_out = demultiplexer_1_out2;  // OR_Gate or_5, 24 bits wide OR_Gate
  assign or_6_out = demultiplexer_1_out3;  // OR_Gate or_6, 24 bits wide OR_Gate
  assign or_7_out = demultiplexer_1_out4;  // OR_Gate or_7, 24 bits wide OR_Gate
  assign or_8_out = demultiplexer_1_out5;  // OR_Gate or_8, 24 bits wide OR_Gate
  assign or_9_out = demultiplexer_1_out6;  // OR_Gate or_9, 24 bits wide OR_Gate
  assign or_10_out = demultiplexer_1_out7;  // OR_Gate or_10, 24 bits wide OR_Gate
  assign or_11_out = demultiplexer_1_out8;  // OR_Gate or_11, 24 bits wide OR_Gate
  assign or_12_out = demultiplexer_1_out9;  // OR_Gate or_12, 24 bits wide OR_Gate
  assign or_13_out = digit_1_c1 | demultiplexer_1_out10;  // OR_Gate or_13, 24 bits wide
  assign or_14_out = digit_1_c2 | demultiplexer_1_out11;  // OR_Gate or_14, 24 bits wide
  assign or_15_out = digit_1_c3 | demultiplexer_1_out12;  // OR_Gate or_15, 24 bits wide
  assign or_16_out = demultiplexer_1_out13;  // OR_Gate or_16, 24 bits wide OR_Gate
  assign or_17_out = demultiplexer_1_out14;  // OR_Gate or_17, 24 bits wide OR_Gate
  assign or_18_out = 24'h555555 | demultiplexer_1_out15;  // OR_Gate or_18, 24 bits wide
  assign or_19_out = demultiplexer_1_out16;  // OR_Gate or_19, 24 bits wide OR_Gate
  assign or_20_out = demultiplexer_1_out17;  // OR_Gate or_20, 24 bits wide OR_Gate
  assign or_21_out = digit_2_c1 | demultiplexer_1_out18;  // OR_Gate or_21, 24 bits wide
  assign or_22_out = digit_2_c2 | demultiplexer_1_out19;  // OR_Gate or_22, 24 bits wide
  assign or_23_out = digit_2_c3 | demultiplexer_1_out20;  // OR_Gate or_23, 24 bits wide
  assign or_24_out = demultiplexer_1_out21;  // OR_Gate or_24, 24 bits wide OR_Gate
  assign or_25_out = demultiplexer_1_out22;  // OR_Gate or_25, 24 bits wide OR_Gate
  assign or_26_out = demultiplexer_1_out23;  // OR_Gate or_26, 24 bits wide OR_Gate
  assign or_27_out = demultiplexer_1_out24;  // OR_Gate or_27, 24 bits wide OR_Gate
  assign or_28_out = demultiplexer_1_out25;  // OR_Gate or_28, 24 bits wide OR_Gate
  assign or_29_out = demultiplexer_1_out26;  // OR_Gate or_29, 24 bits wide OR_Gate
  assign or_30_out = demultiplexer_1_out27;  // OR_Gate or_30, 24 bits wide OR_Gate
  assign or_31_out = demultiplexer_1_out28;  // OR_Gate or_31, 24 bits wide OR_Gate
  assign or_32_out = shifter_3_out | demultiplexer_1_out29;  // OR_Gate or_32, 24 bits wide
  assign or_33_out = {24{1'b0}} | demultiplexer_1_out30;  // OR_Gate or_33, 24 bits wide
  Joystick #(.bits(5)) joystick_2 (.y(B));  // open: x
endmodule

module paddleCtl (
  input  [4:0] JoyY,
  input  Lose,
  output [4:0] PaddleY
);

  wire clock_1_out;
  wire [1:0] comparator_1_gt;
  wire [4:0] not_1_out, subtractor_1_out;
  wire [7:0] adder_1_out, bit_extender_1_out, multiplexer_1_out, register_1_q;

  assign not_1_out = ~JoyY;  // NOT_Gate not_1, 5 bits wide
  // Probe on subtractor_1_out
  Subtractor #(.width(5)) subtractor_1 (.a(not_1_out), .b(5'b01111), .out(subtractor_1_out));  // open: bin, bout
  assign bit_extender_1_out = {{3{subtractor_1_out[4]}}, subtractor_1_out};  // Bit_Extender bit_extender_1
  Comparator comparator_1 (.a(adder_1_out), .b(8'h48), .gt(comparator_1_gt[0]));  // open: eq, lt
  Adder adder_1 (.a(bit_extender_1_out), .b(register_1_q), .out(adder_1_out));  // open: cin, cout
  Comparator comparator_2 (.a(adder_1_out), .b(8'hb8), .lt(comparator_1_gt[1]));  // open: gt, eq
  // Probe on adder_1_out
  Register register_1 (.D(multiplexer_1_out), .en(1'b1), .clk(clock_1_out), .Q(register_1_q), .clr(Lose));
  Multiplexer #(.enable("false"), .select(2), .width(8)) multiplexer_1 (
    .in0(adder_1_out), .in1(8'h48), .in2(8'hb8), .out(multiplexer_1_out), .sel(comparator_1_gt));  // open: in3
  Clock clock_1 (.out(clock_1_out));
  Adder #(.width(5)) adder_2 (.a(5'b01001), .b(register_1_q[7:3]), .out(PaddleY));  // open: cin, cout
endmodule

module truc (
  input  Cond1,
  input  Cond2,
  input  Lose,
  input  Clk,
  input  [13:0] in_5,
  output [4:0] Value
);

  wire comparator_1_eq, or_1_out;
  wire [4:0] adder_1_out, multiplexer_1_out, negator_1_out, register_1_q;

  Negator #(.width(5)) negator_1 (.in(multiplexer_1_out), .out(negator_1_out));
  or or_1 (or_1_out, Cond1, Cond2);
  Register #(.trigger("falling"), .width(5)) register_1 (
    .D(negator_1_out), .en(or_1_out), .clk(Clk), .Q(register_1_q), .clr(Lose));
  // Buzzer #(.waveform("Square")) buzzer_1: pin names not known; wires that end beside it: in_5, or_1_out, {7{1'b1}}
  Comparator #(.width(5)) comparator_1 (.a({5{1'b0}}), .b(register_1_q), .eq(comparator_1_eq));  // open: gt, lt
  Multiplexer #(.enable("false"), .width(5)) multiplexer_1 (
    .in0(register_1_q), .in1(5'b00001), .out(multiplexer_1_out), .sel(comparator_1_eq));
  Register #(.width(5)) register_2 (.D(adder_1_out), .en(1'b1), .clk(Clk), .Q(Value), .clr(Lose));
  Adder #(.width(5)) adder_1 (.a(Value), .b(multiplexer_1_out), .out(adder_1_out));  // open: cin, cout
endmodule

module digit (
  input  [3:0] Score,
  output [23:0] C1,
  output [23:0] C2,
  output [23:0] C3
);

  wire [14:0] rom_1_data;
  wire [23:0] bit_extender_1_out, bit_extender_2_out, bit_extender_3_out;

  ROM #(.addrWidth(4), .dataWidth(15)) rom_1 (.addr(Score), .data(rom_1_data));
  DotMatrix #(.matrixcols(3), .matrixrows(5)) dotmatrix_1 (
    .col0(rom_1_data[4:0]), .col1(rom_1_data[9:5]), .col2(rom_1_data[14:10]));
  assign bit_extender_1_out = {{19{1'b0}}, rom_1_data[4:0]};  // Bit_Extender bit_extender_1
  assign bit_extender_2_out = {{19{1'b0}}, rom_1_data[9:5]};  // Bit_Extender bit_extender_2
  assign bit_extender_3_out = {{19{1'b0}}, rom_1_data[14:10]};  // Bit_Extender bit_extender_3
  Shifter #(.width(24)) shifter_1 (.in(bit_extender_1_out), .\dist (5'b10010), .out(C1));
  Shifter #(.width(24)) shifter_2 (.in(bit_extender_2_out), .\dist (5'b10010), .out(C2));
  Shifter #(.width(24)) shifter_3 (.in(bit_extender_3_out), .\dist (5'b10010), .out(C3));

  // Notes on the sheet:
  //   contents of rom_1 (hex, n*v repeats v):
  //   7e3f 7c00 76b7 7eb5 7c9c 5ebd 5ebf 7e10 7ebf 7ebd 7ebd
endmodule
